# Fritzing sketch 02 servos (saved by Fritzing 0.8.0b)
breadboards: 1

parts:
  Composants1 = Arduino Uno (Rev3)
  LED1 = LED - 5mm [color="Red (633nm)" package="5 mm [THT]"]
  R1 = Resistor [tolerance=±5% resistance=220 package=THT]
  J1 = Basic Servo
  J2 = Basic Servo

nets:
  GND: Composants1.GND, R1.Pin_1, J1.gnd, J2.gnd
  N1: Composants1.D9_PWM, J1.pulse
  N2: Composants1.D10_PWM/SS, J2.pulse
  N3: Composants1.D13/SCK, LED1.anode
  VCC: Composants1.5V, J1.vcc, J2.vcc
  N4: LED1.cathode, R1.Pin_0
