# Fritzing sketch 03.laser (saved by Fritzing 0.8.0b)
breadboards: 1

parts:
  Composants1 = Arduino Uno (Rev3)
  LED1 = LED - 5mm [color="Red (633nm)" package="5 mm [THT]"]
  R1 = Resistor [tolerance=±5% resistance=220 package=THT]
  J1 = Basic Servo
  J2 = Basic Servo
  VCC1 = Battery
  Q1 = NPN-Transistor [package="TO92 [THT]"]
  LED2 = LED - 5mm [color="Red (633nm)" package="5 mm [THT]"]
  R2 = Resistor [tolerance=±5% resistance=560 package="0603 [SMD]"]

nets:
  N1: Composants1.ICSP_MISO, Composants1.D12/MISO, R2.Pin_1
  VCC: Composants1.5V, J1.vcc, J2.vcc, Q1.E
  GND: Composants1.GND, R1.Pin_1, J1.gnd, J2.gnd, VCC1.-
  N2: Composants1.D9_PWM, J1.pulse
  N3: Composants1.D10_PWM/SS, J2.pulse
  N4: Composants1.D13/SCK, LED1.anode
  N5: LED1.cathode, R1.Pin_0
  N6: VCC1.+, LED2.anode
  N7: Q1.B, R2.Pin_0
  N8: Q1.C, LED2.cathode
