# Fritzing sketch 03.laser2 (saved by Fritzing 0.8.0b)
breadboards: 1

parts:
  Composants1 = Arduino Uno (Rev3)
  LED1 = LED - 5mm [color="Red (633nm)" package="5 mm [THT]"]
  R1 = Resistor [tolerance=±5% resistance=220 package=THT]
  J1 = Basic Servo
  J2 = Basic Servo
  VCC1 = Battery
  Q1 = NPN-Transistor [package="TO92 [THT]"]
  LED2 = LED - 5mm [color="Red (633nm)" package="5 mm [THT]"]

nets:
  VCC: Composants1.5V, J1.vcc, J2.vcc, Q1.E
  GND: Composants1.GND, R1.Pin_1, J1.gnd, J2.gnd, VCC1.-
  N1: Composants1.D9_PWM, J1.pulse
  N2: Composants1.D10_PWM/SS, J2.pulse
  N3: Composants1.D12/MISO, Q1.B
  N4: Composants1.D13/SCK, LED1.anode
  N5: LED1.cathode, R1.Pin_0
  N6: VCC1.+, LED2.anode
  N7: Q1.C, LED2.cathode
