# Fritzing sketch 04 simple model (saved by Fritzing 0.8.3b)
breadboards: 1

parts:
  Composants1 = Arduino Uno (Rev3)
  LED1 = LED - 5mm [color="Red (633nm)" package="5 mm [THT]"]
  R1 = Resistor [tolerance=±5% resistance=220 package=THT]
  J1 = Basic Servo
  J2 = Basic Servo
  J3 = Basic Servo

nets:
  N1: Composants1.ICSP_MISO, Composants1.D12/MISO, J3.pulse
  GND: Composants1.GND, R1.Pin_1, J1.gnd, J2.gnd, J3.gnd
  N2: Composants1.D9_PWM, J1.pulse
  N3: Composants1.D10_PWM/SS, J2.pulse
  N4: Composants1.D13/SCK, LED1.anode
  VCC: Composants1.5V, J1.vcc, J2.vcc, J3.vcc
  N5: LED1.cathode, R1.Pin_0
